// Logisim project Datapath.circ as structural Verilog: 16 circuits, main circuit Pipeline_CPU
module Decode_Stage (
  input  [31:0] in_1,
  output [5:0] OPCode,
  output [3:0] Rd,
  output [3:0] Rs,
  output [3:0] Rt,
  output [13:0] Imm
);


  assign Imm = in_1[13:0];
  assign OPCode = in_1[31:26];
  assign Rd = in_1[25:22];
  assign Rs = in_1[21:18];
  assign Rt = in_1[17:14];
endmodule

module RegFile (
  input  [3:0] RA,
  input  [3:0] RB,
  input  [31:0] BusW,
  input  [3:0] RW,
  input  WE,
  input  CLK,
  output [31:0] BusA,
  output [31:0] BusB
);

  wire and_1_out, and_2_out, and_3_out, and_4_out, and_5_out, and_6_out, and_7_out, and_8_out, and_9_out,
       and_10_out, and_11_out, and_12_out, and_13_out, and_14_out, and_15_out, decoder_2_out0,
       decoder_2_out1, decoder_2_out2, decoder_2_out3, decoder_2_out4, decoder_2_out5, decoder_2_out6,
       decoder_2_out7, decoder_2_out8, decoder_2_out9, decoder_2_out10, decoder_2_out11, decoder_2_out12,
       decoder_2_out13, decoder_2_out14, decoder_3_out0, decoder_3_out1, decoder_3_out2, decoder_3_out3,
       decoder_3_out4, decoder_3_out5, decoder_3_out6, decoder_3_out7, decoder_3_out8, decoder_3_out9,
       decoder_3_out10, decoder_3_out11, decoder_3_out12, decoder_3_out13, decoder_3_out14, r0, r1, r2, r3,
       r4, r5, r6, r7, r8, r9, r10, r11, r12, r13, r14;
  wire [31:0] register_1_q, register_2_q, register_3_q, register_4_q, register_5_q, register_6_q,
       register_7_q, register_8_q, register_9_q, register_10_q, register_11_q, register_12_q, register_13_q,
       register_14_q, register_15_q;

  Decoder #(.select(4), .enable("false")) decoder_1 (
    .out0(r0), .out1(r1), .out2(r2), .out3(r3), .out4(r4), .out5(r5), .out6(r6), .out7(r7), .out8(r8),
    .out9(r9), .out10(r10), .out11(r11), .out12(r12), .out13(r13), .out14(r14), .sel(RW));  // open: out15
  and and_1 (and_1_out, r0, WE);
  and and_2 (and_2_out, r1, WE);
  and and_3 (and_3_out, r2, WE);
  and and_4 (and_4_out, r3, WE);
  and and_5 (and_5_out, r4, WE);
  and and_6 (and_6_out, r5, WE);
  and and_7 (and_7_out, r6, WE);
  and and_8 (and_8_out, r7, WE);
  and and_9 (and_9_out, r8, WE);
  and and_10 (and_10_out, r9, WE);
  and and_11 (and_11_out, r10, WE);
  and and_12 (and_12_out, r11, WE);
  and and_13 (and_13_out, r12, WE);
  and and_14 (and_14_out, r13, WE);
  and and_15 (and_15_out, r13, WE);
  Decoder #(.select(4), .enable("false")) decoder_2 (
    .out0(decoder_2_out0), .out1(decoder_2_out1), .out2(decoder_2_out2), .out3(decoder_2_out3),
    .out4(decoder_2_out4), .out5(decoder_2_out5), .out6(decoder_2_out6), .out7(decoder_2_out7),
    .out8(decoder_2_out8), .out9(decoder_2_out9), .out10(decoder_2_out10), .out11(decoder_2_out11),
    .out12(decoder_2_out12), .out13(decoder_2_out13), .out14(decoder_2_out14), .sel(RA));  // open: out15
  assign BusA = decoder_2_out0 ? register_1_q : 32'bz;  // Controlled_Buffer controlled_buffer_1
  Register #(.width(32)) register_1 (.D(BusW), .en(and_1_out), .Q(register_1_q), .clk(CLK));  // open: clr
  Register #(.width(32)) register_2 (.D(BusW), .en(and_2_out), .Q(register_2_q), .clk(CLK));  // open: clr
  Register #(.width(32)) register_3 (.D(BusW), .en(and_3_out), .Q(register_3_q), .clk(CLK));  // open: clr
  Register #(.width(32)) register_4 (.D(BusW), .en(and_4_out), .Q(register_4_q), .clk(CLK));  // open: clr
  Register #(.width(32)) register_5 (.D(BusW), .en(and_5_out), .Q(register_5_q), .clk(CLK));  // open: clr
  Register #(.width(32)) register_6 (.D(BusW), .en(and_6_out), .Q(register_6_q), .clk(CLK));  // open: clr
  Register #(.width(32)) register_7 (.D(BusW), .en(and_7_out), .Q(register_7_q), .clk(CLK));  // open: clr
  Register #(.width(32)) register_8 (.D(BusW), .en(and_8_out), .Q(register_8_q), .clk(CLK));  // open: clr
  Register #(.width(32)) register_9 (.D(BusW), .en(and_9_out), .Q(register_9_q), .clk(CLK));  // open: clr
  assign BusA = decoder_2_out8 ? register_9_q : 32'bz;  // Controlled_Buffer controlled_buffer_2
  Register #(.width(32)) register_10 (.D(BusW), .en(and_10_out), .Q(register_10_q), .clk(CLK));  // open: clr
  assign BusA = decoder_2_out9 ? register_10_q : 32'bz;  // Controlled_Buffer controlled_buffer_3
  assign BusA = decoder_2_out10 ? register_11_q : 32'bz;  // Controlled_Buffer controlled_buffer_4
  Register #(.width(32)) register_11 (.D(BusW), .en(and_11_out), .Q(register_11_q), .clk(CLK));  // open: clr
  assign BusA = decoder_2_out11 ? register_12_q : 32'bz;  // Controlled_Buffer controlled_buffer_5
  Register #(.width(32)) register_12 (.D(BusW), .en(and_12_out), .Q(register_12_q), .clk(CLK));  // open: clr
  Register #(.width(32)) register_13 (.D(BusW), .en(and_13_out), .Q(register_13_q), .clk(CLK));  // open: clr
  assign BusA = decoder_2_out12 ? register_13_q : 32'bz;  // Controlled_Buffer controlled_buffer_6
  Register #(.width(32)) register_14 (.D(BusW), .en(and_14_out), .Q(register_14_q), .clk(CLK));  // open: clr
  assign BusA = decoder_2_out13 ? register_14_q : 32'bz;  // Controlled_Buffer controlled_buffer_7
  Register #(.width(32)) register_15 (.D(BusW), .en(and_15_out), .Q(register_15_q), .clk(CLK));  // open: clr
  assign BusA = decoder_2_out14 ? register_15_q : 32'bz;  // Controlled_Buffer controlled_buffer_8
  assign BusA = decoder_2_out1 ? register_2_q : 32'bz;  // Controlled_Buffer controlled_buffer_9
  assign BusA = decoder_2_out2 ? register_3_q : 32'bz;  // Controlled_Buffer controlled_buffer_10
  assign BusA = decoder_2_out3 ? register_4_q : 32'bz;  // Controlled_Buffer controlled_buffer_11
  assign BusA = decoder_2_out4 ? register_5_q : 32'bz;  // Controlled_Buffer controlled_buffer_12
  assign BusA = decoder_2_out5 ? register_6_q : 32'bz;  // Controlled_Buffer controlled_buffer_13
  assign BusA = decoder_2_out6 ? register_7_q : 32'bz;  // Controlled_Buffer controlled_buffer_14
  assign BusA = decoder_2_out7 ? register_8_q : 32'bz;  // Controlled_Buffer controlled_buffer_15
  assign BusB = decoder_3_out0 ? register_1_q : 32'bz;  // Controlled_Buffer controlled_buffer_16
  assign BusB = decoder_3_out1 ? register_2_q : 32'bz;  // Controlled_Buffer controlled_buffer_17
  assign BusB = decoder_3_out2 ? register_3_q : 32'bz;  // Controlled_Buffer controlled_buffer_18
  assign BusB = decoder_3_out3 ? register_4_q : 32'bz;  // Controlled_Buffer controlled_buffer_19
  assign BusB = decoder_3_out4 ? register_5_q : 32'bz;  // Controlled_Buffer controlled_buffer_20
  assign BusB = decoder_3_out5 ? register_6_q : 32'bz;  // Controlled_Buffer controlled_buffer_21
  assign BusB = decoder_3_out6 ? register_7_q : 32'bz;  // Controlled_Buffer controlled_buffer_22
  assign BusB = decoder_3_out7 ? register_8_q : 32'bz;  // Controlled_Buffer controlled_buffer_23
  assign BusB = decoder_3_out8 ? register_9_q : 32'bz;  // Controlled_Buffer controlled_buffer_24
  assign BusB = decoder_3_out9 ? register_10_q : 32'bz;  // Controlled_Buffer controlled_buffer_25
  assign BusB = decoder_3_out10 ? register_11_q : 32'bz;  // Controlled_Buffer controlled_buffer_26
  assign BusB = decoder_3_out11 ? register_12_q : 32'bz;  // Controlled_Buffer controlled_buffer_27
  assign BusB = decoder_3_out12 ? register_13_q : 32'bz;  // Controlled_Buffer controlled_buffer_28
  assign BusB = decoder_3_out13 ? register_14_q : 32'bz;  // Controlled_Buffer controlled_buffer_29
  assign BusB = decoder_3_out14 ? register_15_q : 32'bz;  // Controlled_Buffer controlled_buffer_30
  Decoder #(.select(4), .enable("false")) decoder_3 (
    .out0(decoder_3_out0), .out1(decoder_3_out1), .out2(decoder_3_out2), .out3(decoder_3_out3),
    .out4(decoder_3_out4), .out5(decoder_3_out5), .out6(decoder_3_out6), .out7(decoder_3_out7),
    .out8(decoder_3_out8), .out9(decoder_3_out9), .out10(decoder_3_out10), .out11(decoder_3_out11),
    .out12(decoder_3_out12), .out13(decoder_3_out13), .out14(decoder_3_out14), .sel(RB));  // open: out15
endmodule

module ALU (
  input  [31:0] IN1,
  input  [31:0] IN2,
  input  [1:0] Alu_opcode,
  output [31:0] Result
);

  wire comparator_1_eq, comparator_1_gt, comparator_1_lt, not_1_out;
  wire [2:0] comparator_2_gt;
  wire [31:0] adder_1_out, adder_2_out, bit_extender_1_out, bit_extender_2_out, bit_extender_3_out,
       multiplexer_1_out, or_1_out, subtractor_1_out;

  Comparator #(.width(32)) comparator_1 (
    .a(IN1), .b(IN2), .gt(comparator_1_gt), .eq(comparator_1_eq), .lt(comparator_1_lt));
  Subtractor #(.width(32)) subtractor_1 (.a(IN1), .b(IN2), .out(subtractor_1_out));  // open: bin, bout
  assign or_1_out = IN1 | IN2;  // OR_Gate or_1, 32 bits wide
  not not_1 (not_1_out, comparator_1_eq);
  assign bit_extender_1_out = {{31{1'b0}}, comparator_1_lt};  // Bit_Extender bit_extender_1
  Comparator #(.width(32)) comparator_2 (
    .a(IN1), .b(IN2), .gt(comparator_2_gt[0]), .eq(comparator_2_gt[1]), .lt(comparator_2_gt[2]));
  Adder #(.width(32)) adder_1 (.a(IN1), .b(IN2), .out(adder_1_out));  // open: cin, cout
  assign bit_extender_2_out = {{31{1'b0}}, comparator_1_gt};  // Bit_Extender bit_extender_2
  assign bit_extender_3_out = {{31{1'b0}}, not_1_out};  // Bit_Extender bit_extender_3
  Adder #(.width(32)) adder_2 (.a(bit_extender_1_out), .b(32'hfffffffe), .out(adder_2_out));  // open: cin, cout
  Multiplexer #(.select(3), .width(32), .enable("false")) multiplexer_1 (
    .in1(bit_extender_2_out), .in2(bit_extender_3_out), .in4(adder_2_out), .out(multiplexer_1_out),
    .sel(comparator_2_gt));  // open: in0, in3, in5, in6, in7
  Multiplexer #(.select(2), .width(32), .disabled(0), .enable("false")) multiplexer_2 (
    .in0(adder_1_out), .in1(subtractor_1_out), .in2(or_1_out), .in3(multiplexer_1_out), .out(Result),
    .sel(Alu_opcode));
endmodule

module PC_ControlUnit (
  input  [31:0] PC,
  input  [31:0] Imm,
  input  ZF,
  input  NF,
  input  [31:0] Reg,
  input  [5:0] Opcode,
  output [31:0] NextPC
);

  wire and_1_out, comparator_1_eq, comparator_2_eq, nand_1_out, not_1_out;
  wire [31:0] adder_1_out, adder_2_out, multiplexer_1_out, multiplexer_2_out, multiplexer_3_out;

  Comparator #(.width(1)) comparator_1 (.a(ZF), .b(1'b1), .eq(comparator_1_eq));  // open: gt, lt
  Comparator #(.width(1)) comparator_2 (.a(NF), .b(1'b1), .eq(comparator_2_eq));  // open: gt, lt
  not not_1 (not_1_out, comparator_1_eq);
  Adder #(.width(32)) adder_1 (.a(PC), .b(32'h1), .out(adder_1_out));  // open: cin, cout
  Adder #(.width(32)) adder_2 (.a(PC), .b(Imm), .out(adder_2_out));  // open: cin, cout
  and and_1 (and_1_out, not_1_out, comparator_2_eq);
  nand nand_1 (nand_1_out, comparator_1_eq, comparator_2_eq);
  Multiplexer #(.width(32), .enable("false")) multiplexer_1 (
    .in0(adder_1_out), .in1(adder_2_out), .out(multiplexer_1_out), .sel(comparator_1_eq));
  Multiplexer #(.width(32), .enable("false")) multiplexer_2 (
    .in0(adder_1_out), .in1(adder_2_out), .out(multiplexer_2_out), .sel(nand_1_out));
  Multiplexer #(.width(32), .enable("false")) multiplexer_3 (
    .in0(adder_1_out), .in1(adder_2_out), .out(multiplexer_3_out), .sel(and_1_out));
  Multiplexer #(.select(4), .width(32), .enable("false")) multiplexer_4 (
    .in0(adder_1_out), .in10(multiplexer_1_out), .in11(multiplexer_2_out), .in12(multiplexer_3_out),
    .in13(Reg), .in14(adder_2_out), .in15(adder_2_out), .out(NextPC), .sel(Opcode[3:0]));  // open: in1, in2, in3, in4, in5, in6, in7, in8, in9
endmodule

module Fetch_Decode (
  input  [31:0] F_Inst,
  input  [31:0] F_PC,
  input  Clk,
  output [31:0] D_Inst,
  output [31:0] D_PC
);

  Register #(.width(32)) register_1 (.D(F_Inst), .Q(D_Inst), .clk(Clk));  // open: en, clr
  Register #(.width(32)) register_2 (.D(F_PC), .Q(D_PC), .clk(Clk));  // open: en, clr
endmodule

module Control_Unit (
  input  [5:0] OPCODE,
  output [5:0] opcode_2,
  output [1:0] WBData,
  output MEM_write,
  output MEM_read,
  output [1:0] ALUOp,
  output ALUSrc,
  output regWrite,
  output Extop,
  output St
);

  wire comparator_1_eq, comparator_2_eq;

  ROM #(.addrWidth(6), .dataWidth(15)) rom_1 (
    .addr(OPCODE), .data({Extop, regWrite, ALUSrc, ALUOp, MEM_read, MEM_write, WBData, opcode_2}));  // open: sel
  Comparator #(.width(6)) comparator_1 (.a(OPCODE), .b(6'b000111), .eq(comparator_1_eq));  // open: gt, lt
  Comparator #(.width(6)) comparator_2 (.a(OPCODE), .b(6'b001001), .eq(comparator_2_eq));  // open: gt, lt
  or or_1 (St, comparator_1_eq, comparator_2_eq);

  // Notes on the sheet:
  //   contents of rom_1 (hex, n*v repeats v):
  //   2800 2000 2400 2c00 3800 7000 7240 5100 7248 5109 400a 400b 400c d 400e 608f
endmodule

module ID_EX (
  input  [3:0] regDest_d,
  input  regWrite_d,
  input  memRead_d,
  input  memWrite_d,
  input  [31:0] src1_d,
  input  [31:0] src2_d,
  input  [31:0] imm_d,
  input  ALU_signal,
  input  [1:0] WBData_d,
  input  [1:0] ALU_op,
  input  [31:0] D_Pc,
  input  check_SDW_d,
  input  check_LDW_d,
  input  count1_d,
  input  count2_d,
  input  CLK,
  output [3:0] regDest_e,
  output regWrite_e,
  output memRead_e,
  output memWrite_e,
  output [31:0] src1_e,
  output [31:0] src2_e,
  output [31:0] imm_e,
  output ALU_signal_2,
  output [1:0] WBData_e,
  output [1:0] ALU_op_2,
  output [31:0] E_Pc,
  output check_SDW_e,
  output check_LDW_e,
  output count1_e,
  output count2_e
);

  Register #(.width(4)) register_1 (.D(regDest_d), .Q(regDest_e), .clk(CLK));  // open: en, clr
  Register #(.width(1)) register_2 (.D(regWrite_d), .Q(regWrite_e), .clk(CLK));  // open: en, clr
  Register #(.width(1)) register_3 (.D(memRead_d), .Q(memRead_e), .clk(CLK));  // open: en, clr
  Register #(.width(1)) register_4 (.D(memWrite_d), .Q(memWrite_e), .clk(CLK));  // open: en, clr
  Register #(.width(32)) register_5 (.D(src1_d), .Q(src1_e), .clk(CLK));  // open: en, clr
  Register #(.width(32)) register_6 (.D(src2_d), .Q(src2_e), .clk(CLK));  // open: en, clr
  Register #(.width(32)) register_7 (.D(imm_d), .Q(imm_e), .clk(CLK));  // open: en, clr
  Register #(.width(1)) register_8 (.D(ALU_signal), .Q(ALU_signal_2), .clk(CLK));  // open: en, clr
  Register #(.width(2)) register_9 (.D(WBData_d), .Q(WBData_e), .clk(CLK));  // open: en, clr
  Register #(.width(2)) register_10 (.D(ALU_op), .Q(ALU_op_2), .clk(CLK));  // open: en, clr
  Register #(.width(32)) register_11 (.D(D_Pc), .Q(E_Pc), .clk(CLK));  // open: en, clr
  Register #(.width(1)) register_12 (.D(check_SDW_d), .Q(check_SDW_e), .clk(CLK));  // open: en, clr
  Register #(.width(1)) register_13 (.D(check_LDW_d), .Q(check_LDW_e), .clk(CLK));  // open: en, clr
  Register #(.width(1)) register_14 (.D(count1_d), .Q(count1_e), .clk(CLK));  // open: en, clr
  Register #(.width(1)) register_15 (.D(count2_d), .Q(count2_e), .clk(CLK));  // open: en, clr
endmodule

module EX_ME (
  input  [3:0] Rd_Ex,
  input  WE_Ex,
  input  MemR_Ex,
  input  MemW_Ex,
  input  [31:0] Data_Ex,
  input  [31:0] Result_Ex,
  input  [1:0] WB_Ex,
  input  [31:0] E_Pc,
  input  Clk,
  output [3:0] Rd_Mem,
  output WE_Mem,
  output MemR_Mem,
  output MemW_Mem,
  output [31:0] Data_Mem,
  output [31:0] Result_Mem,
  output [1:0] WB_Mem,
  output [31:0] M_Pc
);

  Register #(.width(4)) register_1 (.D(Rd_Ex), .Q(Rd_Mem), .clk(Clk));  // open: en, clr
  Register #(.width(1)) register_2 (.D(WE_Ex), .Q(WE_Mem), .clk(Clk));  // open: en, clr
  Register #(.width(1)) register_3 (.D(MemR_Ex), .Q(MemR_Mem), .clk(Clk));  // open: en, clr
  Register #(.width(1)) register_4 (.D(MemW_Ex), .Q(MemW_Mem), .clk(Clk));  // open: en, clr
  Register #(.width(32)) register_5 (.D(Data_Ex), .Q(Data_Mem), .clk(Clk));  // open: en, clr
  Register #(.width(32)) register_6 (.D(Result_Ex), .Q(Result_Mem), .clk(Clk));  // open: en, clr
  Register #(.width(2)) register_7 (.D(WB_Ex), .Q(WB_Mem), .clk(Clk));  // open: en, clr
  Register #(.width(32)) register_8 (.D(E_Pc), .Q(M_Pc), .clk(Clk));  // open: en, clr
endmodule

module MEM_WB (
  input  [3:0] regDest_m,
  input  regWrite_m,
  input  [31:0] WBData_m,
  input  Clk,
  output [3:0] regDest_wb,
  output regWrite_wb,
  output [31:0] WBData_wb
);

  Register #(.width(4)) register_1 (.D(regDest_m), .Q(regDest_wb), .clk(Clk));  // open: en, clr
  Register #(.width(1)) register_2 (.D(regWrite_m), .Q(regWrite_wb), .clk(Clk));  // open: en, clr
  Register #(.width(32)) register_3 (.D(WBData_m), .Q(WBData_wb), .clk(Clk));  // open: en, clr
endmodule

module Forwarding_Unit (
  input  [3:0] R,
  input  [3:0] Rd_Ex,
  input  WE_Ex,
  input  [3:0] Rd_Mem,
  input  WE_Mem,
  input  [3:0] Rd_WB,
  input  WE_WB,
  output [1:0] Forward
);

  wire and_1_out, and_2_out, and_3_out, and_4_out, and_5_out, and_6_out, comparator_1_eq, comparator_2_eq,
       comparator_3_eq, not_1_out, not_2_out;

  Comparator #(.width(4)) comparator_1 (.a(R), .b(Rd_Ex), .eq(comparator_1_eq));  // open: gt, lt
  Comparator #(.width(4)) comparator_2 (.a(R), .b(Rd_Mem), .eq(comparator_2_eq));  // open: gt, lt
  Comparator #(.width(4)) comparator_3 (.a(R), .b(Rd_WB), .eq(comparator_3_eq));  // open: gt, lt
  and and_1 (and_1_out, comparator_1_eq, WE_Ex);
  and and_2 (and_2_out, comparator_2_eq, WE_Mem);
  and and_3 (and_3_out, comparator_3_eq, WE_WB);
  not not_1 (not_1_out, and_1_out);
  not not_2 (not_2_out, and_2_out);
  and and_4 (and_4_out, not_1_out, and_2_out);
  and and_5 (and_5_out, not_1_out, and_3_out);
  and and_6 (and_6_out, not_2_out, and_3_out);
  or or_1 (Forward[0], and_1_out, and_6_out);
  or or_2 (Forward[1], and_4_out, and_5_out);
endmodule

module Stall_Detection (
  input  MEMRead_EX,
  input  [1:0] Forword_B,
  input  [1:0] Forword_A,
  input  [1:0] WB_Data,
  output Stall
);

  wire and_1_out, and_2_out, comparator_1_eq, comparator_2_eq, comparator_3_eq, or_1_out;

  Comparator #(.width(2)) comparator_1 (.a(Forword_B), .b(2'b01), .eq(comparator_1_eq));  // open: gt, lt
  Comparator #(.width(2)) comparator_2 (.a(2'b01), .b(Forword_A), .eq(comparator_2_eq));  // open: gt, lt
  Comparator #(.width(2)) comparator_3 (.a(WB_Data), .b(2'b10), .eq(comparator_3_eq));  // open: gt, lt
  or or_1 (or_1_out, comparator_1_eq, comparator_2_eq);
  and and_1 (and_1_out, MEMRead_EX, or_1_out);
  and and_2 (and_2_out, or_1_out, comparator_3_eq);
  or or_2 (Stall, and_1_out, and_2_out);
endmodule

module Kill_Detection (
  input  [5:0] OPcode,
  input  ZF,
  input  NF,
  output kill
);

  wire and_1_out, and_2_out, and_3_out, comparator_1_eq, comparator_2_eq, comparator_3_eq, comparator_4_eq,
       comparator_5_eq, comparator_6_eq, not_1_out, not_2_out;

  Comparator #(.width(6)) comparator_1 (.a(OPcode), .b(6'b001010), .eq(comparator_1_eq));  // open: gt, lt
  not not_1 (not_1_out, ZF);
  not not_2 (not_2_out, NF);
  Comparator #(.width(6)) comparator_2 (.a(OPcode), .b(6'b001011), .eq(comparator_2_eq));  // open: gt, lt
  Comparator #(.width(6)) comparator_3 (.a(OPcode), .b(6'b001100), .eq(comparator_3_eq));  // open: gt, lt
  Comparator #(.width(6)) comparator_4 (.a(OPcode), .b(6'b001101), .eq(comparator_4_eq));  // open: gt, lt
  Comparator #(.width(6)) comparator_5 (.a(OPcode), .b(6'b001110), .eq(comparator_5_eq));  // open: gt, lt
  Comparator #(.width(6)) comparator_6 (.a(OPcode), .b(6'b001111), .eq(comparator_6_eq));  // open: gt, lt
  and and_1 (and_1_out, comparator_1_eq, ZF);
  and and_2 (and_2_out, not_2_out, not_1_out, comparator_2_eq);
  and and_3 (and_3_out, NF, not_1_out, comparator_3_eq);
  or or_1 (kill, and_1_out, and_2_out, and_3_out, comparator_4_eq, comparator_5_eq, comparator_6_eq);
endmodule

module Pipeline_CPU (
  input  Clk
);

  wire alusrc_d, alusrc_e, and_1_out, and_2_out, and_3_out, and_4_out, count1_d, count1_e, count2_d,
       count2_e, extop_d, insert_NOP, kill, LDW_d, LDW_e, mem_read_d, mem_read_e, mem_read_m, mem_write_d,
       mem_write_e, mem_write_m, NF, or_1_out, or_2_out, regwrite_d, regwrite_e, regwrite_m, regwrite_wb,
       SDW_d, SDW_e, st_d, stall, ZF;
  wire [1:0] aluop_d, aluop_e, forwardA, forwardB, wb_data_d, wb_data_e, wb_data_m;
  wire [3:0] adder_1_out, rd, regDst_d, regDst_e, regDst_m, regDst_wb, rs, rt, rt_sel;
  wire [5:0] Inst_Opcode, opcode, opcodeF_d;
  wire [13:0] imm;
  wire [25:0] rom_1_data;
  wire [31:0] adder_2_out, ALU_res__m, ALU_res_e, bit_extender_1_out, bit_extender_2_out, data_in, data_m,
       data_wb, id_ex_1_src1_e, immExt, immExt_d, immExt_e, in2, in2_ALU, inst, multiplexer_1_out,
       multiplexer_2_out, multiplexer_3_out, multiplexer_4_out, multiplexer_8_out, multiplexer_9_out,
       multiplexer_10_out, pc_controlunit_1_nextpc, pc_d, pc_e, pc_m, PC_q, ram_1_data, rs_data, rt_d_data;

  PC_ControlUnit pc_controlunit_1 (
    .NextPC(pc_controlunit_1_nextpc), .PC(PC_q), .Imm(immExt), .ZF(ZF), .Reg(rs_data), .NF(NF),
    .Opcode(opcodeF_d));
  Multiplexer #(.width(32), .enable("false")) multiplexer_1 (
    .in0(pc_controlunit_1_nextpc), .in1(pc_d), .out(multiplexer_1_out), .sel(stall));
  Register #(.width(32)) PC (.D(multiplexer_1_out), .Q(PC_q), .clk(Clk));  // open: en, clr
  ROM #(.addrWidth(24), .dataWidth(32)) rom_1 (.addr(PC_q[23:0]), .data({Inst_Opcode, rom_1_data}));  // open: sel
  Insert_NOP insert_nop_1 (.Opcode(Inst_Opcode), .Clk(Clk), .insert_NOP(insert_NOP));
  Multiplexer #(.width(32), .enable("false")) multiplexer_2 (
    .in0(multiplexer_4_out), .in1({32{1'b0}}), .out(multiplexer_2_out), .sel(kill));
  Multiplexer #(.width(32), .enable("false")) multiplexer_3 (
    .in0(multiplexer_2_out), .in1(inst), .out(multiplexer_3_out), .sel(insert_NOP));
  Multiplexer #(.width(32), .enable("false")) multiplexer_4 (
    .in0({Inst_Opcode, rom_1_data}), .in1(inst), .out(multiplexer_4_out), .sel(stall));
  Fetch_Decode fetch_decode_1 (
    .F_Inst(multiplexer_3_out), .F_PC(multiplexer_1_out), .D_Inst(inst), .D_PC(pc_d), .Clk(Clk));
  Control_Unit control_unit_1 (
    .OPCODE(opcode), .regWrite(regwrite_d), .MEM_read(mem_read_d), .MEM_write(mem_write_d),
    .WBData(wb_data_d), .ALUSrc(alusrc_d), .opcode_2(opcodeF_d), .Extop(extop_d), .ALUOp(aluop_d), .St(st_d));
  Adder #(.width(4)) adder_1 (.a(rd), .b(4'b0001), .out(adder_1_out));  // open: cin, cout
  assign bit_extender_1_out = {{18{1'b0}}, imm};  // Bit_Extender bit_extender_1
  Multiplexer #(.width(32), .enable("false")) multiplexer_5 (
    .in0(bit_extender_1_out), .in1(bit_extender_2_out), .out(immExt_d), .sel(extop_d));
  assign bit_extender_2_out = {{18{imm[13]}}, imm};  // Bit_Extender bit_extender_2
  and and_1 (and_1_out, SDW_d, count1_d);
  or or_1 (or_1_out, and_1_out, and_2_out);
  and and_2 (and_2_out, LDW_d, count2_d);
  Multiplexer #(.width(4), .enable("false")) multiplexer_6 (
    .in0(rd), .in1(adder_1_out), .out(regDst_d), .sel(or_1_out));
  Multiplexer #(.width(4), .enable("false")) multiplexer_7 (.in0(rt), .in1(regDst_d), .out(rt_sel), .sel(st_d));
  Decode_Stage decode_stage_1 (.OPCode(opcode), .Rd(rd), .in_1(inst), .Rt(rt), .Rs(rs), .Imm(imm));
  Forwarding_Unit forwarding_unit_1 (
    .R(rs), .Rd_Ex(regDst_e), .Rd_Mem(regDst_m), .Rd_WB(regDst_wb), .WE_Ex(regwrite_e), .WE_Mem(regwrite_m),
    .WE_WB(regwrite_wb), .Forward(forwardA));
  Kill_Detection kill_detection_1 (.OPcode(opcodeF_d), .kill(kill), .NF(NF), .ZF(ZF));
  comparator comparator_1 (.R(rs_data), .NF(NF), .ZF(ZF));
  RegFile regfile_1 (
    .RA(rs), .RB(rt_sel), .BusW(data_wb), .RW(regDst_wb), .WE(regwrite_wb), .CLK(Clk), .BusA(rs_data),
    .BusB(rt_d_data));
  ldw_sdw ldw_sdw_1 (
    .Opcode(opcode), .checkLDW(LDW_d), .count2(count2_d), .checkSDW(SDW_d), .count1(count1_d), .Clk(Clk));
  Stall_Detection stall_detection_1 (
    .MEMRead_EX(mem_read_e), .Forword_A(forwardA), .Forword_B(forwardB), .Stall(stall), .WB_Data(wb_data_m));
  Multiplexer #(.select(2), .width(32), .enable("false")) multiplexer_8 (
    .in0(rs_data), .in1(ALU_res_e), .in2(data_m), .in3(data_wb), .out(multiplexer_8_out), .sel(forwardA));
  Multiplexer #(.select(2), .width(32), .enable("false")) multiplexer_9 (
    .in0(rt_d_data), .in1(ALU_res_e), .in2(data_m), .in3(data_wb), .out(multiplexer_9_out), .sel(forwardB));
  Forwarding_Unit forwarding_unit_2 (
    .R(rt_sel), .Rd_Ex(regDst_e), .Rd_Mem(regDst_m), .Rd_WB(regDst_wb), .WE_Ex(regwrite_e),
    .WE_Mem(regwrite_m), .WE_WB(regwrite_wb), .Forward(forwardB));
  ID_EX id_ex_1 (
    .regDest_d(regDst_d), .regWrite_d(regwrite_d), .memRead_d(mem_read_d), .memWrite_d(mem_write_d),
    .src1_d(multiplexer_8_out), .src2_d(multiplexer_9_out), .ALU_signal(alusrc_d), .WBData_d(wb_data_d),
    .regDest_e(regDst_e), .regWrite_e(regwrite_e), .memRead_e(mem_read_e), .memWrite_e(mem_write_e),
    .src1_e(id_ex_1_src1_e), .src2_e(in2), .ALU_signal_2(alusrc_e), .WBData_e(wb_data_e), .imm_d(immExt_d),
    .imm_e(immExt_e), .CLK(Clk), .ALU_op(aluop_d), .ALU_op_2(aluop_e), .D_Pc(pc_d), .E_Pc(pc_e),
    .check_SDW_d(SDW_d), .check_SDW_e(SDW_e), .check_LDW_d(LDW_d), .check_LDW_e(LDW_e), .count1_d(count1_d),
    .count1_e(count1_e), .count2_d(count2_d), .count2_e(count2_e));
  ALU alu_1 (.IN1(id_ex_1_src1_e), .IN2(in2_ALU), .Result(ALU_res_e), .Alu_opcode(aluop_e));
  Adder #(.width(32)) adder_2 (.a(immExt_e), .b(32'h1), .out(adder_2_out));  // open: cin, cout
  and and_3 (and_3_out, SDW_e, count1_e);
  and and_4 (and_4_out, LDW_e, count2_e);
  Multiplexer #(.width(32), .enable("false")) multiplexer_10 (
    .in0(immExt_e), .in1(adder_2_out), .out(multiplexer_10_out), .sel(or_2_out));
  or or_2 (or_2_out, and_3_out, and_4_out);
  Multiplexer #(.width(32), .enable("false")) multiplexer_11 (
    .in0(in2), .in1(multiplexer_10_out), .out(in2_ALU), .sel(alusrc_e));
  EX_ME ex_me_1 (
    .Rd_Ex(regDst_e), .WE_Ex(regwrite_e), .MemR_Ex(mem_read_e), .MemW_Ex(mem_write_e), .Data_Ex(in2),
    .Result_Ex(ALU_res_e), .WB_Ex(wb_data_e), .Clk(Clk), .Rd_Mem(regDst_m), .WE_Mem(regwrite_m),
    .MemR_Mem(mem_read_m), .MemW_Mem(mem_write_m), .Data_Mem(data_in), .Result_Mem(ALU_res__m),
    .WB_Mem(wb_data_m), .E_Pc(pc_e), .M_Pc(pc_m));
  RAM #(.addrWidth(24), .dataWidth(32), .bus("separate")) ram_1 (
    .addr(ALU_res__m[23:0]), .din(data_in), .data(ram_1_data), .str(mem_write_m), .clk(Clk), .ld(mem_read_m));  // open: sel, clr
  Multiplexer #(.select(2), .width(32), .enable("false")) multiplexer_12 (
    .in0(ALU_res__m), .in1(ram_1_data), .in2(pc_m), .out(data_m), .sel(wb_data_m));  // open: in3
  MEM_WB mem_wb_1 (
    .regDest_m(regDst_m), .regWrite_m(regwrite_m), .WBData_m(data_m), .Clk(Clk), .regDest_wb(regDst_wb),
    .regWrite_wb(regwrite_wb), .WBData_wb(data_wb));

  // Notes on the sheet:
  //   contents of rom_1 (hex, n*v repeats v):
  //   1400000a 14400014 24240000
endmodule

module ldw_sdw (
  input  [5:0] Opcode,
  input  Clk,
  output checkLDW,
  output count2,
  output checkSDW,
  output count1
);

  wire comparator_1_eq, comparator_2_eq;

  Comparator #(.width(6)) comparator_1 (.a(Opcode), .b(6'b001000), .eq(comparator_1_eq));  // open: gt, lt
  Comparator #(.width(6)) comparator_2 (.a(Opcode), .b(6'b001001), .eq(comparator_2_eq));  // open: gt, lt
  Register #(.width(1)) register_1 (.D(comparator_1_eq), .Q(checkLDW), .clk(Clk));  // open: en, clr
  Register #(.width(1)) register_2 (.D(comparator_2_eq), .Q(checkSDW), .clk(Clk));  // open: en, clr

  assign count1 = checkSDW;
  assign count2 = checkLDW;
endmodule

module comparator (
  input  [31:0] R,
  output ZF,
  output NF
);

  Comparator #(.width(32)) comparator_1 (.a(R), .b({32{1'b0}}), .eq(ZF), .lt(NF));  // open: gt
endmodule

module Insert_NOP (
  input  [5:0] Opcode,
  input  Clk,
  output insert_NOP
);

  wire comparator_1_eq, comparator_2_eq, or_1_out;

  Comparator #(.width(6)) comparator_1 (.a(Opcode), .b(6'b001000), .eq(comparator_1_eq));  // open: gt, lt
  Comparator #(.width(6)) comparator_2 (.a(Opcode), .b(6'b001001), .eq(comparator_2_eq));  // open: gt, lt
  Register #(.width(1)) register_1 (.D(or_1_out), .Q(insert_NOP), .clk(Clk));  // open: en, clr
  or or_1 (or_1_out, comparator_1_eq, comparator_2_eq);
endmodule
